# Fritzing sketch PlacaWEB (saved by Fritzing 0.9.2b)
circuit board: 5.85715cm x 8.74687cm

parts:
  M2 = Stepper Motor - Bipolar
  MD09B2 = A4988 Stepper Motor Driver Carrier
  MD09B3 = A4988 Stepper Motor Driver Carrier
  Blutooth = Bluetooth JY-MCU
  C1 = Electrolytic Capacitor [capacitance=1µF package="100 mil [THT, electrolytic]"]
  C2 = Electrolytic Capacitor [capacitance=1µF package="100 mil [THT, electrolytic]"]
  J12 = Screw terminal - 2 pins [package=THT]
  J13 = Screw terminal - 2 pins [package=THT]
  J14 = Screw terminal - 2 pins [package=THT]
  J15 = Screw terminal - 2 pins [package=THT]
  R1 = Resistor [tolerance=±5% resistance=220 package=THT]
  R2 = Resistor [tolerance=±5% resistance=4.7k package=THT]
  R3 = Resistor [tolerance=±5% resistance=220 package=THT]
  R4 = Resistor [tolerance=±5% resistance=220 package=THT]
  R5 = Resistor [tolerance=±5% resistance=220 package=THT]
  R6 = Resistor [tolerance=±5% resistance=220 package=THT]
  R7 = Resistor [tolerance=±5% resistance=220 package=THT]
  R8 = Resistor [tolerance=±5% resistance=220 package=THT]
  J16 = Screw terminal - 2 pins [package=THT]
  M1 = Stepper Motor - Bipolar
  R9 = Resistor [tolerance=±5% resistance=220 package=THT]
  R10 = Resistor [tolerance=±5% resistance=220 package=THT]
  R11 = Resistor [tolerance=±5% resistance=220 package=THT]
  R12 = Resistor [tolerance=±5% resistance=220 package=THT]
  Part4 = Arduino Due (Rev2b)

nets:
  N1: M2.A, MD09B3.OUT_2B
  N2: M2.C, MD09B3.OUT_2A
  N3: M2.B, MD09B3.OUT_1A
  N4: M2.D, MD09B3.OUT_1B
  N5: MD09B2.Enable, Part4.D52
  N6: MD09B2.MS1, Part4.D50
  N7: MD09B2.MS2, Part4.D48
  N8: MD09B2.MS3, Part4.D46
  N9: MD09B2.RESET, Part4.D44
  N10: MD09B2.SLEEP, Part4.D42
  N11: MD09B2.STEP, Part4.D40
  N12: MD09B2.DIR, Part4.D38
  N13: MD09B2.VMOT, MD09B3.VMOT, C1.+, C2.+, J12.pin2
  GND: MD09B2.GROUND, MD09B3.GROUND, Blutooth.GND, C1.-, C2.-, J12.pin1, J13.pin1, R5.Pin_0, R6.Pin_0, R7.Pin_0, R8.Pin_0, R9.Pin_0, R10.Pin_0, Part4.GND
  N14: MD09B2.OUT_2B, M1.A
  N15: MD09B2.OUT_2A, M1.C
  N16: MD09B2.OUT_1A, M1.B
  N17: MD09B2.OUT_1B, M1.D
  VDD: MD09B2.VDD, MD09B3.VDD, Blutooth.VCC_5V, J13.pin2, Part4.5V
  N18: MD09B3.Enable, Part4.D36
  N19: MD09B3.MS1, Part4.D34
  N20: MD09B3.MS2, Part4.D32
  N21: MD09B3.MS3, Part4.D30
  N22: MD09B3.RESET, Part4.D28
  N23: MD09B3.SLEEP, Part4.D26
  N24: MD09B3.STEP, Part4.D24
  N25: MD09B3.DIR, Part4.D22
  N26: Blutooth.RX_3.3V, Part4.D14/TX3
  N27: Blutooth.TX_3.3V, Part4.D15/RX3
  N28: J14.pin1, R3.Pin_1, R8.Pin_1
  N29: J14.pin2, R2.Pin_1, R7.Pin_1
  N30: J15.pin1, R4.Pin_1, R5.Pin_1
  N31: J15.pin2, R1.Pin_1, R6.Pin_1
  N32: R1.Pin_0, Part4.D9_PWM
  N33: R2.Pin_0, Part4.D7_PWM
  N34: R3.Pin_0, Part4.D8_PWM
  N35: R4.Pin_0, Part4.D10_PWM/SS0
  N36: J16.pin1, R10.Pin_1, R12.Pin_1
  N37: J16.pin2, R9.Pin_1, R11.Pin_1
  N38: R11.Pin_0, Part4.D11_PWM
  N39: R12.Pin_0, Part4.D12_PWM

notes:
  RA
  DEC
  12V-24V
  -
  B1 B2
  A1  A2
  A1 A2
  +
  5V

custom parts:
  Bluetooth JY-MCU: Description: The Bluetooth Mate is very similar to our BlueSMiRF modem, but it is designed specifically to be used with our Arduino Pros and LilyPad Arduinos. These modems work as a serial (RX/TX) pipe, and are a great wireless replacement for serial cables. Any serial stream from 9600 to 115200bps can be passed seamlessly from your computer to your target. Bluetooth Mate has the same pin out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
